# Fritzing sketch esp8266_12f_flash (saved by Fritzing 0.9.5d)

parts:
  ESP8266-1 = ESP8266-12 [part_number=ESP8266-12]
  Part1 = FTDI Basic Programmer

nets:
  N1: ESP8266-1.GPIO13, ESP8266-1.VCC, Part1.POWER
  N2: ESP8266-1.TXD, Part1.RXI
  N3: ESP8266-1.RXD, ESP8266-1.GPIO5, Part1.TXO
  GND: ESP8266-1.GPIO15, ESP8266-1.GND, Part1.GND

notes:
  3.3 V
  connect while flashing
