# Fritzing sketch current (saved by Fritzing 0.9.3b)
breadboards: 2

parts:
  U2 = NodeMCU V1.0
  Part1 = INA219 High Side DC Current Sensor Breakout [part_number=904]
  Part2 = Adafruit Micro USB Breakout [part_number="Adafruit #1833"]
  ESP8266-1 = ESP8266-12 [part_number=ESP8266-12]

nets:
  N1: U2.D1, Part1.SCL
  N2: U2.D2, Part1.SDA
  3V3: U2.3V3, Part1.VCC
  GND: U2.GND, Part1.GND, Part2.GND, ESP8266-1.GND
  N3: Part1.VIN-, Part2.VBUS
  N4: Part1.VIN+, ESP8266-1.VCC

notes:
  Circuit to Measure

custom parts:
  NodeMCU V1.0: ESP8266 based NodeMCU
  INA219 High Side DC Current Sensor Breakout: This breakout board will solve all your power-monitoring problems. Instead of struggling with two multimeters, you can just use the handy INA219B chip on this breakout to both measure both the high side voltage and DC current draw over I2C with 1% precision. Most current-measuring devices such as our current panel meter are only good for low side measuring. That means that unless you want to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
  Adafruit Micro USB Breakout: Simple but effective - this breakout board has a USB Micro-B connector, with all 5 pins broken out. Great for pairing with a microcontroller with USB support, or adding USB 5V power to a project. We use a micro-AB connector with through-hole shielding pads for an excellent strong connection - it won't rip off by accident! Comes with one fully assembled and tested micro B breakout PCB and a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
