# Fritzing sketch remote (saved by Fritzing 0.9.3b)
breadboards: 1

parts:
  U1 = NodeMCU V1.0
  LED1 = LEDs [package=led10mm]
  Q1 = NPN-Transistor [package="TO92 [THT]"]
  R1 = Resistor [tolerance=±5% resistance=220 package="0603 [SMD]"]

nets:
  N1: U1.D0, R1.Pin_1
  N2: U1.3V3, LED1.A
  N3: U1.GND, Q1.C
  N4: LED1.C, Q1.E
  N5: Q1.B, R1.Pin_0

custom parts:
  NodeMCU V1.0: ESP8266 based NodeMCU
