# Fritzing sketch temperature (saved by Fritzing 0.9.3b)
breadboards: 1

parts:
  U1 = NodeMCU
  RHT1 = Humidity and Temperature Sensor RHT03
  R1 = Resistor [tolerance=±5% resistance=10k package="2512 [SMD]"]

nets:
  N1: U1.connector7, RHT1.Data-signal, R1.Pin_0
  N2: U1.connector16, RHT1.GND_2
  N3: U1.connector19, RHT1.Vcc, R1.Pin_1
